# Fritzing sketch HarMan-shield (saved by Fritzing 0.9.3b)
circuit board: 10cm x 6.72cm
circuit board: 2.5cm x 1.8cm
circuit board: 4cm x 2.4cm
circuit board: 2.39511cm x 6.72889cm
breadboards: 1

parts:
  CHAN_SEL1 = male pin header, 5 pins [form="♂ (male)"]
  MIDI_IN = male pin header, 2 pins [form="♂ (male)"]
  9V1 = male pin header, 2 pins [form="♂ (male)"]
  IN = male pin header, 4 pins [form="♂ (male)"]
  SWITCH = male pin header, 2 pins [form="♂ (male)"]
  1 = male pin header, 1 pin [form="♂ (male)"]
  ISP = male pin header, 6 pins [form="♂ (male)"]
  J1 = male pin header, 4 pins [form="♂ (male)"]
  J2 = female pin header, 4 pins [form="♀ (female)"]
  J3 = male pin header, 4 pins [form="♂ (male)"]
  J4 = female pin header, 4 pins [form="♀ (female)"]
  J12 = male pin header, 3 pins [form="♂ (male)"]
  J11 = female pin header, 3 pins [form="♀ (female)"]
  J14 = male pin header, 6 pins [form="♂ (male)"]
  J13 = female pin header, 6 pins [form="♀ (female)"]
  J16 = male pin header, 5 pins [form="♂ (male)"]
  J15 = female pin header, 5 pins [form="♀ (female)"]
  Pro_Micro1 = Arduino Pro Micro
  R3 = Resistor [tolerance=±5% resistance=220 package=THT]
  LED3 = LED - 3mm [color="Red (633nm)" package="3 mm [THT]"]
  LED2 = LED - 3mm [color="Red (633nm)" package="3 mm [THT]"]
  LED1 = LED - 3mm [color="Red (633nm)" package="3 mm [THT]"]
  R1 = Resistor [tolerance=±5% resistance=220 package=THT]
  R2 = Resistor [tolerance=±5% resistance=220 package=THT]
  DIN1 = DIN-5 jack (MIDI) [part_number=DS-5-01 package=THTw]
  Power_plug1 = Power plug [part_number=DS-210]
  S1 = Pushbutton [package="[THT]"]
  LED4 = LED - 3mm [color="Red (633nm)" package="3 mm [THT]"]
  LED5 = LED - 3mm [color="Red (633nm)" package="3 mm [THT]"]
  LED6 = LED - 3mm [color="Red (633nm)" package="3 mm [THT]"]
  LED7 = LED - 3mm [color="Red (633nm)" package="3 mm [THT]"]
  R4 = Resistor [tolerance=±5% resistance=220 package=THT]
  R5 = Resistor [tolerance=±5% resistance=220 package=THT]
  R6 = Resistor [tolerance=±5% resistance=220 package=THT]
  R7 = Resistor [tolerance=±5% resistance=220 package=THT]
  IN1 = male pin header, 4 pins [form="♂ (male)"]
  MIDI_SW = male pin header, 4 pins [form="♂ (male)"]
  9V = male pin header, 3 pins [form="♂ (male)"]
  ISP1 = male pin header, 6 pins [form="♂ (male)"]
  CHAN_SEL2 = male pin header, 5 pins [form="♂ (male)"]
  SW1 = DIP SWITCH [package=dipswitch-02]
  SW2 = DIP SWITCH [package=dipswitch-02]
  ISP_VCC = female pin header, 2 pins [form="♀ (female)"]
  J17 = female pin header, 1 pin [form="♀ (female)"]
  J18 = female pin header, 1 pin [form="♀ (female)"]
  J19 = female pin header, 1 pin [form="♀ (female)"]
  CHAN_SEL3 = male pin header, 5 pins [form="♂ (male)"]
  SW3 = DIP SWITCH [package=dipswitch-02]
  SW4 = DIP SWITCH [package=dipswitch-02]
  Mini-DIN1 = Mini-DIN-6 [package=THT]
  J20 = female pin header, 6 pins [form="♀ (female)"]

nets:
  N1: CHAN_SEL1.pin1, CHAN_SEL2.pin1, SW2.3
  N2: CHAN_SEL1.pin2, CHAN_SEL2.pin2, SW2.4
  N3: CHAN_SEL1.pin3, CHAN_SEL2.pin3, SW1.3
  N4: CHAN_SEL1.pin4, CHAN_SEL2.pin4, SW1.4
  N5: CHAN_SEL1.pin5, CHAN_SEL2.pin5, SW1.1, SW1.2, SW2.1, SW2.2, J17.pin1
  N6: MIDI_IN.pin1, DIN1.5, MIDI_SW.pin4
  N7: MIDI_IN.pin2, DIN1.4, MIDI_SW.pin3
  N8: 9V1.pin1, Power_plug1.VCC, 9V.pin3
  GND: 9V1.pin2, SWITCH.pin2, ISP.pin2, Pro_Micro1.GND, LED3.cathode, LED2.cathode, LED1.cathode, Power_plug1.GND, S1.Pin_1, S1.Pin_2, LED4.cathode, LED5.cathode, LED6.cathode, LED7.cathode, MIDI_SW.pin1, 9V.pin2, ISP1.pin2
  N9: IN.pin1, LED4.anode, R4.Pin_1, IN1.pin1
  N10: IN.pin2, LED5.anode, R5.Pin_1, IN1.pin2
  N11: IN.pin3, LED6.anode, R6.Pin_1, IN1.pin3
  N12: IN.pin4, LED7.anode, R7.Pin_1, IN1.pin4
  N13: SWITCH.pin1, Pro_Micro1.A0, S1.Pin_3, S1.Pin_4, MIDI_SW.pin2, J18.pin1, J19.pin1
  N14: 1.pin1, 9V.pin1
  N15: ISP.pin1, ISP1.pin1, ISP_VCC.pin2
  N16: ISP.pin3, Pro_Micro1.D6_PWM, ISP1.pin3
  N17: ISP.pin4, Pro_Micro1.D7, ISP1.pin4
  N18: ISP.pin5, Pro_Micro1.D8, ISP1.pin5
  N19: ISP.pin6, Pro_Micro1.D9_PWM, ISP1.pin6
  N20: J1.pin1, J2.pin1
  N21: J1.pin2, J2.pin2
  N22: J1.pin3, J2.pin3
  N23: J1.pin4, J2.pin4
  N24: J3.pin1, J4.pin1
  N25: J3.pin2, J4.pin2
  N26: J3.pin3, J4.pin3
  N27: J3.pin4, J4.pin4
  N28: J12.pin1, J11.pin1
  N29: J12.pin2, J11.pin2
  N30: J12.pin3, J11.pin3
  N31: J14.pin1, J13.pin1
  N32: J14.pin2, J13.pin2
  N33: J14.pin3, J13.pin3
  N34: J14.pin4, J13.pin4
  N35: J14.pin5, J13.pin5
  N36: J14.pin6, J13.pin6
  N37: J16.pin1, J15.pin1
  N38: J16.pin2, J15.pin2
  N39: J16.pin3, J15.pin3
  N40: J16.pin4, J15.pin4
  N41: J16.pin5, J15.pin5
  N42: Pro_Micro1.D3_PWM, R3.Pin_0
  N43: Pro_Micro1.D4, R2.Pin_0
  N44: Pro_Micro1.D5_PWM, R1.Pin_0
  N45: Pro_Micro1.5V, ISP_VCC.pin1
  N46: Pro_Micro1.D13, R7.Pin_0
  N47: Pro_Micro1.D12, R6.Pin_0
  N48: Pro_Micro1.D11_PWM, R5.Pin_0
  N49: Pro_Micro1.D10_PWM, R4.Pin_0
  N50: R3.Pin_1, LED3.anode
  N51: LED2.anode, R2.Pin_1
  N52: LED1.anode, R1.Pin_1
  N53: CHAN_SEL3.pin1, SW4.3
  N54: CHAN_SEL3.pin2, SW4.4
  N55: CHAN_SEL3.pin3, SW3.3
  N56: CHAN_SEL3.pin4, SW3.4
  N57: CHAN_SEL3.pin5, SW3.1, SW3.2, SW4.1, SW4.2
  N58: Mini-DIN1.3, J20.pin1
  N59: Mini-DIN1.5, J20.pin2
  N60: Mini-DIN1.2, J20.pin3
  N61: Mini-DIN1.4, J20.pin4
  N62: Mini-DIN1.1, J20.pin5
  N63: Mini-DIN1.GND, J20.pin6

custom parts:
  Arduino Pro Micro: The Arduino Pro Micro is a small microcontroller board originally based on the 32U4
  DIN-5 jack (MIDI): Female DIN connector with 5 pins, as used for MIDI and SYNC
  Power plug: power plug
  Mini-DIN-6: Female Mini-DIN connector with 6 pins
