# Fritzing sketch HarMan-v4 (saved by Fritzing 0.9.3b)
circuit board: 8.4cm x 4.9cm
breadboards: 1

parts:
  6N138 = 6N138 DIP - 8 pins [package="DIP (Dual Inline) [THT]"]
  MIDI_IN = DIN-5 jack (MIDI) [part_number=DS-5-01 package=THTw]
  D1 = Rectifier Diode [part_number=1N4001 package="300 mil [THT]"]
  R1 = Resistor [tolerance=±5% resistance=220 package=THT]
  R2 = Resistor [tolerance=±5% resistance=470 package=THT]
  R3 = Resistor [tolerance=±5% resistance=10k package=THT]
  9v = Power plug [part_number=DS-210]
  VR = Voltage Regulator [package=to220-adj]
  C4 = Tantalum Capacitor [capacitance=10µF voltage=16V package="200 mil [THT, tantalum]"]
  C3 = Tantalum Capacitor [capacitance=10µF voltage=16V package="200 mil [THT, tantalum]"]
  IN = male pin header, 4 pins [form="♂ (male)"]
  9V = male pin header, 2 pins [form="♂ (male)"]
  part = male pin header, 1 pin [form="♂ (male)"]  # not connected
  SWITCH = male pin header, 2 pins [form="♂ (male)"]
  MIDI_IN_2 = male pin header, 2 pins [form="♂ (male)"]
  ISP = male pin header, 6 pins [form="♂ (male)"]
  U1 = 74HC165 [package="DIP16 [THT]"]
  E = female pin header, 1 pin [form="♀ (female)"]
  C = female pin header, 1 pin [form="♀ (female)"]
  B = female pin header, 1 pin [form="♀ (female)"]
  C_2 = female pin header, 1 pin [form="♀ (female)"]
  D = female pin header, 1 pin [form="♀ (female)"]
  E_2 = female pin header, 1 pin [form="♀ (female)"]
  A = female pin header, 1 pin [form="♀ (female)"]
  A_2 = female pin header, 1 pin [form="♀ (female)"]
  B_2 = female pin header, 1 pin [form="♀ (female)"]
  D_2 = female pin header, 1 pin [form="♀ (female)"]
  R4 = Resistor [tolerance=±5% resistance=33k package=THT]
  R5 = Resistor [tolerance=±5% resistance=33k package=THT]
  R6 = Resistor [tolerance=±5% resistance=33k package=THT]
  R7 = Resistor [tolerance=±5% resistance=33k package=THT]
  CHAN_SEL = male pin header, 5 pins [form="♂ (male)"]
  ATtiny84 = ATtiny84 [package="DIP14 [THT]"]

nets:
  N1: 6N138.pin2, D1.cathode, R1.Pin_1
  N2: 6N138.pin3, MIDI_IN.5, D1.anode, MIDI_IN_2.pin1
  GND: 6N138.pin5, R3.Pin_1, 9v.GND, VR.ADJ, C4.-, C3.-, 9V.pin2, SWITCH.pin2, ISP.pin2, U1.E, U1.F, U1.G, U1.H, U1.GND, U1.SER, U1.CLK_INH, R4.Pin_1, R5.Pin_1, R6.Pin_1, R7.Pin_1, ATtiny84.GND
  MIDI IN: 6N138.pin6, R2.Pin_1, ATtiny84.PB1
  N3: 6N138.pin7, R3.Pin_0
  3.3V: 6N138.pin8, R2.Pin_0, VR.OUT, C3.+, ISP.pin1, U1.VCC, CHAN_SEL.pin5, ATtiny84.VCC
  N4: MIDI_IN.4, R1.Pin_0, MIDI_IN_2.pin2
  9V: 9v.VCC, VR.IN, C4.+, 9V.pin1
  in1: IN.pin1, ATtiny84.PA0
  in2: IN.pin2, ATtiny84.PA1
  in3: IN.pin3, ATtiny84.PA2
  in4: IN.pin4, ATtiny84.PA3
  N5: SWITCH.pin1, A.pin1, A_2.pin1, ATtiny84.PB0
  RST: ISP.pin3, B.pin1, B_2.pin1, ATtiny84.PB3
  LD/SCL: ISP.pin4, U1.SH/LD, C.pin1, C_2.pin1, ATtiny84.PA4
  MOSI: ISP.pin5, D.pin1, D_2.pin1, ATtiny84.PA6
  CLK/MISO: ISP.pin6, U1.CLK, E.pin1, E_2.pin1, ATtiny84.PA5
  DATA: U1.QH, ATtiny84.PB2
  N6: U1.A, R7.Pin_0, CHAN_SEL.pin4
  N7: U1.B, R6.Pin_0, CHAN_SEL.pin3
  N8: U1.C, R5.Pin_0, CHAN_SEL.pin2
  N9: U1.D, R4.Pin_0, CHAN_SEL.pin1

notes:
  1 2 3 4      G S 4+5-
  -9v
  +9v
  VCC
  GND
  RST
  SCK
  MOSI
  MISO

custom parts:
  6N138 DIP - 8 pins: A DIP stand-in part for whatever IC you want. With 8 pins on a 300mil dual inline package (DIP) footprint.
  DIN-5 jack (MIDI): Female DIN connector with 5 pins, as used for MIDI and SYNC
  Power plug: power plug
  Voltage Regulator: Voltage Regulator Standard LM317 adjustable voltage regulator. AOI (Adjust Output Input). Google 'LM317 Calculator' for easy to use app to get the two resistor values needed. 240/720 for 5V output. 240/390 for 3.3V output. Spark Fun Electronics SKU : COM-00527
  74HC165: 8-bit parallel-load shift registers
  ATtiny84: Atmel ATtiny84 microcontroller. So small but so powerfull.
